# Fritzing sketch aereni (saved by Fritzing 0.9.8b)

parts:
  U1 = ESP8266 NodeMCU LoLin module
  M1 = BME280
  SDS1 = SDS011 - dust sensor [part_number=1]

nets:
  N1: U1.D1, SDS1.TX
  N2: U1.D2, SDS1.RX
  N3: U1.D3, M1.SDA
  N4: U1.D4, M1.SCL
  3V3: U1.3V3, M1.VIN
  GND: U1.GND, M1.GND, SDS1.GND
  VIN: U1.Vin, SDS1.5v

custom parts:
  ESP8266 NodeMCU LoLin module: ESP8266 based NodeMCU
  BME280: Temperature Humidity Barometric presure Sensor
  SDS011 - dust sensor: The SDS 011 Sensor is a quite recent Air Quality Sensor developed by inovafit, a spin-off from the university of Jinan (in Shandong). With its size, it is probably one of the best sensor in terms of accuracy: While other sensors tend to focus on shrinking the sensor size, the SDS 011 has opted for a size tradeoff allowing it to use a larger fan. And the larger the fan, the better the quality.
